# Fritzing sketch MiniStatPerfboard (saved by Fritzing 0.9.1b)
circuit board: 14.9644cm x 8.92795cm
perfboards: 1

parts:
  U1 = Cypress CY8CKIT-049-42xx PSoC4 prototyping board [part_number=CY8CKIT-049-42xx package=THT]
  LED1 = LED - 5mm [color="Red (633nm)" package="5 mm [THT]"]
  Q1 = LTR-301 [part_number="Osram SFH213" package=ltr-301]
  R1 = Resistor [tolerance=±5% resistance=100k package=THT]
  R3 = Resistor [tolerance=±5% resistance=2k package=THT]
  JP1 = Header 2 [package=molex-1x2_lock]
  JP3 = Header 3 [package=molex-1x3_lock]
  R4 = Resistor [tolerance=±5% resistance=1k package=THT]
  R2 = Resistor [tolerance=±5% resistance=120 package=THT]
  R5 = Resistor [tolerance=±5% resistance=270 package=THT]
  C1 = Ceramic Capacitor [capacitance=100nF package="100 mil [THT, multilayer]"]
  R6 = Resistor [tolerance=±5% resistance=1k package=THT]
  U2 = mystery part, 6 pins [chip_label="6 pin connector"]
  IC1 = ULN2003A [package="SO16 [SMD]"]
  U3 = mystery part, 4 pins [chip_label="4 pin connector"]
  R7 = Resistor [tolerance=±5% resistance=10k package=THT]

nets:
  N1: U1.pin_1, JP3.3, R4.Pin_1, R2.Pin_1, R5.Pin_0, C1.0, R6.Pin_0, IC1.0V
  N2: U1.pin_3, C1.1, R6.Pin_1, U2.pin2
  N3: U1.pin_4, R3.Pin_1, R4.Pin_0
  N4: U1.pin_14, IC1.In_1
  N5: U1.pin_15, IC1.In_2, IC1.In_3
  N6: U1.pin_16, IC1.In_4
  N7: U1.pin_21, U1.pin_35, Q1.E
  N8: U1.pin_36, Q1.C, R1.Pin_1
  N9: U1.pin_37, R1.Pin_0
  N10: U1.pin_38, LED1.anode, R3.Pin_0
  N11: U1.pin_39, LED1.cathode, R2.Pin_0
  N12: U1.pin_40, U1.pin_42
  N13: U1.pin_44, U2.pin3, R7.Pin_1
  N14: JP1.1, IC1.Out_1
  N15: JP1.2, JP3.2, U2.pin6, IC1.COM_-_Common, U3.pin2
  N16: R5.Pin_1, U2.pin1
  N17: U2.pin5, IC1.Out_3, IC1.Out_2
  N18: IC1.Out_4, U3.pin1
  N19: U3.pin4, R7.Pin_0

notes:
  stir motor
  pump &
  sensor
  12V

custom parts:
  Cypress CY8CKIT-049-42xx PSoC4 prototyping board: Prototyping dev board for Cypress CY8C4245 PSoC4
